# Fritzing sketch Lesson27b_Schematic (saved by Fritzing 0.9.3b)
breadboards: 1

parts:
  Launchpad2 = TI Launchpad MSP430G2
  Part1 = TRRS 3.5mm Jack Breakout  # not connected
  R1 = Trimmer Potentiometer [maximum_resistance=10kΩ package=THT]

nets:
  N1: Launchpad2.p14, R1.leg1
  N2: Launchpad2.p20, R1.leg2
